// Logisim project Gameover test.circ as structural Verilog: 1 circuit, main circuit main
module main (
  input  [23:0] in_1,
  input  [23:0] in_2,
  input  [23:0] in_3,
  input  [23:0] in_4,
  input  [23:0] in_5,
  input  [23:0] in_6,
  input  [23:0] in_7,
  input  [23:0] in_8,
  input  [23:0] in_9,
  input  [23:0] in_10
);

  DotMatrix #(.inputtype("row"), .matrixcols(24), .matrixrows(32)) dotmatrix_1 (
    .row12(in_1), .row13(in_2), .row14(in_3), .row15(in_4), .row16(in_5), .row18(in_6), .row19(in_7),
    .row20(in_8), .row21(in_9), .row22(in_10));  // open: row0, row1, row2, row3, row4, row5, row6, row7, row8, row9, row10, row11, row17, row23, row24, row25, row26, row27, row28, row29, row30, row31
endmodule
