// Logisim project Gravity module testing.circ as structural Verilog: 1 circuit, main circuit main
module main (
  input  [7:0] Surrounding,
  input  [7:0] in_2,
  input  [7:0] in_3,
  output [7:0] _3_top_rows,
  output [7:0] out_5
);

  wire comparator_1_gt, not_1_out, not_2_out;
  wire [7:0] controlled_buffer_1_out, controlled_buffer_2_out;

  Comparator comparator_1 (.a(in_3), .b(8'h2), .gt(comparator_1_gt));  // open: eq, lt
  not not_1 (not_1_out, comparator_1_gt);
  assign controlled_buffer_1_out = not_1_out ? Surrounding : 8'bz;  // Controlled_Buffer controlled_buffer_1
  assign _3_top_rows = controlled_buffer_1_out | controlled_buffer_2_out;  // OR_Gate or_1, 8 bits wide
  assign controlled_buffer_2_out = comparator_1_gt ? in_2 : 8'bz;  // Controlled_Buffer controlled_buffer_2
  assign out_5 = not_2_out ? in_2 : 8'bz;  // Controlled_Buffer controlled_buffer_3
  not not_2 (not_2_out, comparator_1_gt);

  // Notes on the sheet:
  //   The second digit counter
  //   The character
  //   3 bottom rows
endmodule
