// Logisim project main.circ as structural Verilog: 8 circuits, main circuit main
module main (
  output [3:0] out_1,
  output [6:0] out_2
);

  wire and_1_out, and_2_out, and_3_out, and_4_out, and_5_out, buffer_1_out, button_1_out, clock_1_out,
       clock_2_out, comparator_1_eq, comparator_2_eq, comparator_4_eq, comparator_4_gt, comparator_5_eq,
       comparator_6_eq, comparator_7_eq, d_ff_1_q, d_ff_2_q, d_ff_3_q, f_obstacle_1_out_6,
       f_obstacle_1_out_7, f_obstacle_2_out_6, f_obstacle_2_out_7, gravity_1_out_3, n7segmentdecoder_1_a_2,
       n7segmentdecoder_1_b_2, n7segmentdecoder_1_c_2, n7segmentdecoder_1_d_2, n7segmentdecoder_1_e,
       n7segmentdecoder_1_f, n7segmentdecoder_1_g, n7segmentdecoder_2_a_2, n7segmentdecoder_2_b_2,
       n7segmentdecoder_2_c_2, n7segmentdecoder_2_d_2, n7segmentdecoder_2_e, n7segmentdecoder_2_f,
       n7segmentdecoder_2_g, n7segmentdecoder_3_a_2, n7segmentdecoder_3_b_2, n7segmentdecoder_3_c_2,
       n7segmentdecoder_3_d_2, n7segmentdecoder_3_e, n7segmentdecoder_3_f, n7segmentdecoder_3_g,
       n7segmentdecoder_4_a_2, n7segmentdecoder_4_b_2, n7segmentdecoder_4_c_2, n7segmentdecoder_4_d_2,
       n7segmentdecoder_4_e, n7segmentdecoder_4_f, n7segmentdecoder_4_g, nor_1_out, nor_2_out, not_1_out,
       not_2_out, not_3_out, not_4_out, not_5_out, not_6_out, obstacle_1_out_6, obstacle_1_out_7,
       obstacle_2_out_6, obstacle_2_out_7, or_1_out, or_2_out, or_3_out, or_4_out, or_5_out, or_6_out,
       or_7_out, or_8_out, or_9_out, or_10_out, or_11_out, scorestopper_1_out_2;
  wire [3:0] adder_1_out, adder_4_out, adder_5_out, adder_6_out, counter_1_q, register_2_q, register_3_q;
  wire [23:0] adder_2_out, adder_3_out, controlled_buffer_1_out, controlled_buffer_3_out, f_obstacle_1_out_5,
       f_obstacle_2_out_5, gameovermodule_1_out_2, gameovermodule_1_out_3, gameovermodule_1_out_4,
       gameovermodule_1_out_5, gameovermodule_1_out_6, gameovermodule_1_out_7, gameovermodule_1_out_8,
       gameovermodule_1_out_9, gameovermodule_1_out_10, gameovermodule_1_out_11, gameovermodule_1_out_12,
       gravity_selector_1_out_7, gravity_selector_1_out_8, gravity_selector_1_out_9,
       gravity_selector_1_out_10, gravity_selector_1_out_11, gravity_selector_2_out_7,
       gravity_selector_2_out_8, gravity_selector_2_out_9, gravity_selector_2_out_10,
       gravity_selector_2_out_11, obstacle_1_out_5, obstacle_2_out_5;

  Clock clock_1 (.out(clock_1_out));
  nor nor_1 (nor_1_out, button_1_out, gravity_1_out_3);
  nor nor_2 (nor_2_out, gravity_1_out_3, button_1_out);
  or or_1 (or_1_out, button_1_out, gravity_1_out_3);
  or or_2 (or_2_out, button_1_out, gravity_1_out_3);
  Keyboard keyboard_1 (.clk(clock_1_out), .clr(and_2_out), .data(out_2));  // open: re, avail
  Button button_1 (.out(button_1_out));
  Adder #(.width(4)) adder_1 (.a(counter_1_q), .b(4'b0001), .out(adder_1_out));  // open: cin, cout
  assign controlled_buffer_1_out = not_1_out ? {24{1'b0}} : 24'bz;  // Controlled_Buffer controlled_buffer_1
  not not_1 (not_1_out, or_8_out);
  assign controlled_buffer_1_out = or_8_out ? 24'h100000 : 24'bz;  // Controlled_Buffer controlled_buffer_2
  Obstacle obstacle_1 (
    .in_1(or_8_out), .in_2(f_obstacle_1_out_7), .in_3(nor_1_out), .out_5(obstacle_1_out_5),
    .out_6(obstacle_1_out_6), .out_7(obstacle_1_out_7));  // open: out_4
  F__Obstacle f_obstacle_1 (
    .in_1(or_6_out), .in_2(obstacle_1_out_7), .in_3(nor_2_out), .out_5(f_obstacle_1_out_5),
    .out_6(f_obstacle_1_out_6), .out_7(f_obstacle_1_out_7));  // open: out_4
  F__Obstacle f_obstacle_2 (
    .in_1(or_8_out), .in_2(obstacle_2_out_7), .in_3(or_1_out), .out_5(f_obstacle_2_out_5),
    .out_6(f_obstacle_2_out_6), .out_7(f_obstacle_2_out_7));  // open: out_4
  Obstacle obstacle_2 (
    .in_1(or_6_out), .in_2(f_obstacle_2_out_7), .in_3(or_2_out), .out_5(obstacle_2_out_5),
    .out_6(obstacle_2_out_6), .out_7(obstacle_2_out_7));  // open: out_4
  assign controlled_buffer_3_out = not_2_out ? {24{1'b0}} : 24'bz;  // Controlled_Buffer controlled_buffer_3
  not not_2 (not_2_out, or_6_out);
  assign controlled_buffer_3_out = or_6_out ? 24'h100000 : 24'bz;  // Controlled_Buffer controlled_buffer_4
  and and_1 (and_1_out, button_1_out, comparator_4_eq);
  Adder #(.width(24)) adder_2 (.a({24{1'b0}}), .b(controlled_buffer_1_out), .out(adder_2_out));  // open: cin, cout
  Adder #(.width(24)) adder_3 (.a({24{1'b0}}), .b(controlled_buffer_3_out), .out(adder_3_out));  // open: cin, cout
  buf buffer_1 (buffer_1_out, and_2_out);
  and and_2 (and_2_out, d_ff_3_q, or_4_out);
  and and_3 (and_3_out, button_1_out, not_3_out);
  not not_3 (not_3_out, button_1_out);
  or or_3 (or_3_out, obstacle_1_out_6, f_obstacle_2_out_6, obstacle_2_out_6, f_obstacle_1_out_6);
  or or_4 (or_4_out, obstacle_1_out_7, obstacle_2_out_7, f_obstacle_2_out_7, f_obstacle_1_out_7);
  Comparator #(.width(7)) comparator_1 (.a(out_2), .b(7'b1110111), .eq(comparator_1_eq));  // open: gt, lt
  Comparator #(.width(7)) comparator_2 (.a(out_2), .b(7'b1110011), .eq(comparator_2_eq));  // open: gt, lt
  Comparator #(.width(7)) comparator_3 (.a(out_2), .b(7'b1100100));  // open: gt, eq, lt
  and and_4 (and_4_out, or_4_out, not_4_out);
  not not_4 (not_4_out, or_4_out);
  Counter #(.width(4), .max('h9), .ongoal("stay"), .trigger("falling")) counter_1 (
    .load(or_4_out), .D(adder_1_out), .Q(counter_1_q), .clk(or_5_out), .clr(and_3_out));  // open: count, carry
  or or_5 (or_5_out, and_1_out, and_4_out, and_5_out);
  ScoreStopper scorestopper_1 (.in_1(out_1), .out_2(scorestopper_1_out_2));
  and and_5 (and_5_out, scorestopper_1_out_2, not_5_out);
  not not_5 (not_5_out, scorestopper_1_out_2);
  Gravity_Selector gravity_selector_1 (
    .in_1(obstacle_1_out_5), .in_2(obstacle_1_out_5), .in_3(f_obstacle_1_out_5), .in_4(adder_2_out),
    .in_5(adder_2_out), .in_6(not_6_out), .out_7(gravity_selector_1_out_7), .out_8(gravity_selector_1_out_8),
    .out_9(gravity_selector_1_out_9), .out_10(gravity_selector_1_out_10), .out_11(gravity_selector_1_out_11));
  not not_6 (not_6_out, gravity_1_out_3);
  Gravity_Selector gravity_selector_2 (
    .in_1(adder_3_out), .in_2(adder_3_out), .in_3(f_obstacle_2_out_5), .in_4(obstacle_2_out_5),
    .in_5(obstacle_2_out_5), .in_6(gravity_1_out_3), .out_7(gravity_selector_2_out_7),
    .out_8(gravity_selector_2_out_8), .out_9(gravity_selector_2_out_9), .out_10(gravity_selector_2_out_10),
    .out_11(gravity_selector_2_out_11));
  Clock clock_2 (.out(clock_2_out));
  DotMatrix #(.inputtype("row"), .matrixcols(24), .matrixrows(32)) dotmatrix_1 (
    .row0({24{1'b1}}), .row1({24{1'b1}}), .row2({24{1'b1}}), .row3({24{1'b1}}), .row4({24{1'b1}}),
    .row5(gravity_selector_1_out_7), .row6(gravity_selector_1_out_8), .row7(gravity_selector_1_out_9),
    .row8(gravity_selector_1_out_10), .row9(gravity_selector_1_out_11), .row10(gameovermodule_1_out_2),
    .row11(gameovermodule_1_out_3), .row12(gameovermodule_1_out_4), .row13(gameovermodule_1_out_5),
    .row14(gameovermodule_1_out_6), .row15(gameovermodule_1_out_7), .row16(gameovermodule_1_out_8),
    .row17(gameovermodule_1_out_9), .row18(gameovermodule_1_out_10), .row19(gameovermodule_1_out_11),
    .row20(gameovermodule_1_out_12), .row21({24{1'b0}}), .row22(gravity_selector_2_out_7),
    .row23(gravity_selector_2_out_8), .row24(gravity_selector_2_out_9), .row25(gravity_selector_2_out_10),
    .row26(gravity_selector_2_out_11), .row27({24{1'b1}}), .row28({24{1'b1}}), .row29({24{1'b1}}),
    .row30({24{1'b1}}), .row31({24{1'b1}}));
  GameOverModule gameovermodule_1 (
    .in_1(buffer_1_out), .out_2(gameovermodule_1_out_2), .out_3(gameovermodule_1_out_3),
    .out_4(gameovermodule_1_out_4), .out_5(gameovermodule_1_out_5), .out_6(gameovermodule_1_out_6),
    .out_7(gameovermodule_1_out_7), .out_8(gameovermodule_1_out_8), .out_9(gameovermodule_1_out_9),
    .out_10(gameovermodule_1_out_10), .out_11(gameovermodule_1_out_11), .out_12(gameovermodule_1_out_12));
  or or_6 (or_6_out, d_ff_1_q, comparator_1_eq);
  D_Flip_Flop d_ff_1 (.clk(clock_2_out), .D(comparator_1_eq), .Q(d_ff_1_q));  // open: Qn, preset, en, reset
  D_Flip_Flop d_ff_2 (.clk(clock_2_out), .D(comparator_2_eq), .Q(d_ff_2_q));  // open: Qn, preset, en, reset
  D_Flip_Flop d_ff_3 (.clk(and_4_out), .D(comparator_4_eq), .Q(d_ff_3_q), .reset(or_7_out));  // open: Qn, preset, en
  or or_7 (or_7_out, button_1_out, comparator_4_gt);
  Comparator #(.width(4)) comparator_4 (
    .a(counter_1_q), .b(4'b0000), .gt(comparator_4_gt), .eq(comparator_4_eq));  // open: lt
  _7SegmentDecoder u_7segmentdecoder_1 (
    .D(counter_1_q[3]), .C(counter_1_q[2]), .B(counter_1_q[1]), .A(counter_1_q[0]),
    .a_2(n7segmentdecoder_1_a_2), .b_2(n7segmentdecoder_1_b_2), .c_2(n7segmentdecoder_1_c_2),
    .d_2(n7segmentdecoder_1_d_2), .e(n7segmentdecoder_1_e), .f(n7segmentdecoder_1_f), .g(n7segmentdecoder_1_g));
  or or_8 (or_8_out, d_ff_2_q, comparator_2_eq);
  _7_Segment_Display u_7_segment_display_1 (
    .g(n7segmentdecoder_1_g), .f(n7segmentdecoder_1_f), .a(n7segmentdecoder_1_a_2),
    .b(n7segmentdecoder_1_b_2), .e(n7segmentdecoder_1_e), .d(n7segmentdecoder_1_d_2),
    .c(n7segmentdecoder_1_c_2));  // open: dp
  Register #(.width(4)) register_1 (.D(adder_4_out), .Q(out_1), .clk(or_3_out), .clr(or_9_out));  // open: en
  Adder #(.width(4)) adder_4 (.a(out_1), .b(4'b0001), .out(adder_4_out));  // open: cin, cout
  or or_9 (or_9_out, comparator_5_eq, button_1_out);
  Comparator #(.width(4)) comparator_5 (.a(out_1), .b(4'b1010), .eq(comparator_5_eq));  // open: gt, lt
  Adder #(.width(4)) adder_5 (.a(register_2_q), .b(4'b0001), .out(adder_5_out));  // open: cin, cout
  Register #(.width(4)) register_2 (
    .D(adder_5_out), .Q(register_2_q), .clk(comparator_5_eq), .clr(or_10_out));  // open: en
  or or_10 (or_10_out, comparator_6_eq, button_1_out);
  Comparator #(.width(4)) comparator_6 (.a(register_2_q), .b(4'b1010), .eq(comparator_6_eq));  // open: gt, lt
  Register #(.width(4)) register_3 (
    .D(adder_6_out), .Q(register_3_q), .clk(comparator_6_eq), .clr(or_11_out));  // open: en
  Adder #(.width(4)) adder_6 (.a(register_3_q), .b(4'b0001), .out(adder_6_out));  // open: cin, cout
  or or_11 (or_11_out, comparator_7_eq, button_1_out);
  Comparator #(.width(4)) comparator_7 (.a(register_3_q), .b(4'b1010), .eq(comparator_7_eq));  // open: gt, lt
  Gravity gravity_1 (.in_1(out_1), .in_2(button_1_out), .out_3(gravity_1_out_3));
  _7SegmentDecoder u_7segmentdecoder_2 (
    .D(register_3_q[3]), .C(register_3_q[2]), .B(register_3_q[1]), .A(register_3_q[0]),
    .a_2(n7segmentdecoder_2_a_2), .b_2(n7segmentdecoder_2_b_2), .c_2(n7segmentdecoder_2_c_2),
    .d_2(n7segmentdecoder_2_d_2), .e(n7segmentdecoder_2_e), .f(n7segmentdecoder_2_f), .g(n7segmentdecoder_2_g));
  _7_Segment_Display u_7_segment_display_2 (
    .g(n7segmentdecoder_2_g), .f(n7segmentdecoder_2_f), .a(n7segmentdecoder_2_a_2),
    .b(n7segmentdecoder_2_b_2), .e(n7segmentdecoder_2_e), .d(n7segmentdecoder_2_d_2),
    .c(n7segmentdecoder_2_c_2));  // open: dp
  _7SegmentDecoder u_7segmentdecoder_3 (
    .D(register_2_q[3]), .C(register_2_q[2]), .B(register_2_q[1]), .A(register_2_q[0]),
    .a_2(n7segmentdecoder_3_a_2), .b_2(n7segmentdecoder_3_b_2), .c_2(n7segmentdecoder_3_c_2),
    .d_2(n7segmentdecoder_3_d_2), .e(n7segmentdecoder_3_e), .f(n7segmentdecoder_3_f), .g(n7segmentdecoder_3_g));
  _7_Segment_Display u_7_segment_display_3 (
    .g(n7segmentdecoder_3_g), .f(n7segmentdecoder_3_f), .a(n7segmentdecoder_3_a_2),
    .b(n7segmentdecoder_3_b_2), .e(n7segmentdecoder_3_e), .d(n7segmentdecoder_3_d_2),
    .c(n7segmentdecoder_3_c_2));  // open: dp
  _7_Segment_Display u_7_segment_display_4 (
    .g(n7segmentdecoder_4_g), .f(n7segmentdecoder_4_f), .a(n7segmentdecoder_4_a_2),
    .b(n7segmentdecoder_4_b_2), .e(n7segmentdecoder_4_e), .d(n7segmentdecoder_4_d_2),
    .c(n7segmentdecoder_4_c_2));  // open: dp
  _7SegmentDecoder u_7segmentdecoder_4 (
    .D(out_1[3]), .C(out_1[2]), .B(out_1[1]), .A(out_1[0]), .a_2(n7segmentdecoder_4_a_2),
    .b_2(n7segmentdecoder_4_b_2), .c_2(n7segmentdecoder_4_c_2), .d_2(n7segmentdecoder_4_d_2),
    .e(n7segmentdecoder_4_e), .f(n7segmentdecoder_4_f), .g(n7segmentdecoder_4_g));

  // Notes on the sheet:
  //   Character
  //   Start / Restart
  //   Flying obstacle
  //   Ground Obstacle
  //   Click to Control [W/S]
  //   W
  //   S
  //   D
  //   Connect Score Board Module Here
  //   Boudnary
  //   D Forward currently disabled
  //   Decrease when 1
  //   Delay
  //   Life
  //   Score
endmodule

module F__Obstacle (
  input  in_1,
  input  in_2,
  input  in_3,
  output [4:0] out_4,
  output [23:0] out_5,
  output out_6,
  output out_7
);

  wire adder_4_out, and_1_out, clock_1_out, clock_2_out, comparator_1_eq, comparator_2_gt, comparator_2_lt,
       comparator_3_eq, comparator_4_eq, comparator_5_eq, comparator_6_eq, comparator_6_gt,
       controlled_buffer_1_out, d_ff_1_q, not_1_out, not_2_out, or_1_out, or_2_out, or_3_out, or_4_out,
       or_5_out;
  wire [3:0] random_1_out;
  wire [4:0] adder_1_out;
  wire [23:0] adder_2_out, controlled_buffer_2_out, shifter_1_out;

  Clock clock_1 (.out(clock_1_out));
  Random #(.width(4)) random_1 (.clk(clock_1_out), .out(random_1_out));  // open: next, clr
  Adder #(.width(5)) adder_1 (.a(out_4), .b(5'b00001), .out(adder_1_out));  // open: cin, cout
  Clock clock_2 (.out(clock_2_out));
  D_Flip_Flop d_ff_1 (.clk(clock_2_out), .D(or_1_out), .Q(d_ff_1_q));  // open: Qn, preset, en, reset
  or or_1 (or_1_out, in_3, d_ff_1_q);
  or or_2 (or_2_out, in_3, comparator_3_eq);
  and and_1 (and_1_out, controlled_buffer_1_out, not_1_out, or_4_out);
  assign controlled_buffer_1_out = d_ff_1_q ? clock_2_out : 1'bz;  // Controlled_Buffer controlled_buffer_1
  not not_1 (not_1_out, or_3_out);
  or or_3 (or_3_out, in_2, out_7);
  Comparator #(.width(4)) comparator_1 (.a(random_1_out), .b(4'b1000), .eq(comparator_1_eq));  // open: gt, lt
  Counter #(.width(5), .max('h18), .ongoal("continue")) counter_1 (
    .D(adder_1_out), .Q(out_4), .clk(and_1_out), .clr(or_2_out));  // open: load, count, carry
  or or_4 (or_4_out, comparator_1_eq, or_5_out);
  Comparator #(.width(5)) comparator_2 (
    .a(out_4), .b({5{1'b0}}), .gt(comparator_2_gt), .lt(comparator_2_lt));  // open: eq
  Comparator #(.width(5)) comparator_3 (.a(out_4), .b(5'b11000), .eq(comparator_3_eq));  // open: gt, lt
  or or_5 (or_5_out, comparator_2_gt, comparator_2_lt);
  assign controlled_buffer_2_out = not_2_out ? 24'h100000 : 24'bz;  // Controlled_Buffer controlled_buffer_2
  not not_2 (not_2_out, in_1);
  Shifter #(.width(24)) shifter_1 (.in(24'h1), .\dist (out_4), .out(shifter_1_out));
  assign controlled_buffer_2_out = in_1 ? {24{1'b0}} : 24'bz;  // Controlled_Buffer controlled_buffer_3
  Adder #(.width(24)) adder_2 (.a({24{1'b0}}), .b(controlled_buffer_2_out), .out(adder_2_out));  // open: cin, cout
  Comparator #(.width(24)) comparator_4 (.a(adder_2_out), .b(24'h100000), .eq(comparator_4_eq));  // open: gt, lt
  Adder #(.width(24)) adder_3 (.a(shifter_1_out), .b(adder_2_out), .out(out_5));  // open: cin, cout
  Adder #(.width(1)) adder_4 (.a(out_6), .b(1'b1), .out(adder_4_out));  // open: cin, cout
  Register #(.width(1)) register_1 (
    .D(adder_4_out), .Q(out_6), .clk(comparator_6_gt), .clr(comparator_5_eq));  // open: en
  Comparator #(.width(1)) comparator_5 (.a(out_6), .b(1'b1), .eq(comparator_5_eq));  // open: gt, lt
  Comparator #(.width(24)) comparator_6 (
    .a(out_5), .b(24'h200000), .gt(comparator_6_gt), .eq(comparator_6_eq));  // open: lt
  and and_2 (out_7, comparator_4_eq, comparator_6_eq);

  // Notes on the sheet:
  //   Chances current 1 in 15
endmodule

module Obstacle (
  input  in_1,
  input  in_2,
  input  in_3,
  output [4:0] out_4,
  output [23:0] out_5,
  output out_6,
  output out_7
);

  wire adder_4_out, and_1_out, clock_1_out, clock_2_out, comparator_1_eq, comparator_2_gt, comparator_2_lt,
       comparator_3_eq, comparator_4_eq, comparator_5_eq, comparator_6_eq, comparator_6_gt,
       controlled_buffer_1_out, d_ff_1_q, not_1_out, not_2_out, or_1_out, or_2_out, or_3_out, or_4_out,
       or_5_out;
  wire [3:0] random_1_out;
  wire [4:0] adder_1_out;
  wire [23:0] adder_2_out, controlled_buffer_2_out, shifter_1_out;

  Clock clock_1 (.out(clock_1_out));
  Random #(.width(4)) random_1 (.clk(clock_1_out), .out(random_1_out));  // open: next, clr
  Adder #(.width(5)) adder_1 (.a(out_4), .b(5'b00001), .out(adder_1_out));  // open: cin, cout
  Clock clock_2 (.out(clock_2_out));
  D_Flip_Flop d_ff_1 (.clk(clock_2_out), .D(or_1_out), .Q(d_ff_1_q));  // open: Qn, preset, en, reset
  or or_1 (or_1_out, in_3, d_ff_1_q);
  or or_2 (or_2_out, in_3, comparator_3_eq);
  and and_1 (and_1_out, controlled_buffer_1_out, not_1_out, or_3_out);
  assign controlled_buffer_1_out = d_ff_1_q ? clock_2_out : 1'bz;  // Controlled_Buffer controlled_buffer_1
  not not_1 (not_1_out, or_4_out);
  or or_3 (or_3_out, comparator_1_eq, or_5_out);
  or or_4 (or_4_out, in_2, out_7);
  Comparator #(.width(4)) comparator_1 (.a(random_1_out), .b(4'b0100), .eq(comparator_1_eq));  // open: gt, lt
  Counter #(.width(5), .max('h18), .ongoal("continue")) counter_1 (
    .D(adder_1_out), .Q(out_4), .clk(and_1_out), .clr(or_2_out));  // open: load, count, carry
  Comparator #(.width(5)) comparator_2 (
    .a(out_4), .b({5{1'b0}}), .gt(comparator_2_gt), .lt(comparator_2_lt));  // open: eq
  Comparator #(.width(5)) comparator_3 (.a(out_4), .b(5'b11000), .eq(comparator_3_eq));  // open: gt, lt
  or or_5 (or_5_out, comparator_2_gt, comparator_2_lt);
  assign controlled_buffer_2_out = not_2_out ? 24'h100000 : 24'bz;  // Controlled_Buffer controlled_buffer_2
  not not_2 (not_2_out, in_1);
  Shifter #(.width(24)) shifter_1 (.in(24'h1), .\dist (out_4), .out(shifter_1_out));
  assign controlled_buffer_2_out = in_1 ? {24{1'b0}} : 24'bz;  // Controlled_Buffer controlled_buffer_3
  Adder #(.width(24)) adder_2 (.a({24{1'b0}}), .b(controlled_buffer_2_out), .out(adder_2_out));  // open: cin, cout
  Adder #(.width(24)) adder_3 (.a(shifter_1_out), .b(adder_2_out), .out(out_5));  // open: cin, cout
  Comparator #(.width(24)) comparator_4 (.a(adder_2_out), .b(24'h100000), .eq(comparator_4_eq));  // open: gt, lt
  Register #(.width(1)) register_1 (
    .D(adder_4_out), .Q(out_6), .clk(comparator_6_gt), .clr(comparator_5_eq));  // open: en
  Adder #(.width(1)) adder_4 (.a(out_6), .b(1'b1), .out(adder_4_out));  // open: cin, cout
  Comparator #(.width(1)) comparator_5 (.a(out_6), .b(1'b1), .eq(comparator_5_eq));  // open: gt, lt
  Comparator #(.width(24)) comparator_6 (
    .a(out_5), .b(24'h200000), .gt(comparator_6_gt), .eq(comparator_6_eq));  // open: lt
  and and_2 (out_7, comparator_4_eq, comparator_6_eq);

  // Notes on the sheet:
  //   Chances current 1 in 15
endmodule

module _7SegmentDecoder (
  input  D,
  input  C,
  input  B,
  input  A,
  output a_2,
  output b_2,
  output c_2,
  output d_2,
  output e,
  output f,
  output g
);

  wire nand_1_out, nand_2_out, nand_3_out, nand_4_out, nand_5_out, nand_6_out, nand_7_out, nand_8_out,
       nand_9_out, nand_10_out, nand_11_out, nand_12_out, nand_13_out, nand_14_out, nand_15_out, nand_16_out,
       nand_17_out, nand_18_out, nand_19_out, nand_20_out, nand_21_out, nand_22_out, nand_23_out,
       nand_24_out, nand_25_out, nand_26_out, nand_27_out, nand_28_out, nand_29_out, nand_30_out,
       nand_31_out, nand_32_out, nand_33_out, nand_34_out, nand_35_out, nand_36_out, nand_37_out,
       nand_38_out, nand_39_out, nand_40_out, nand_41_out, nand_42_out, nand_43_out, nand_44_out,
       nand_45_out, nand_46_out, nand_47_out, nand_48_out, nand_49_out, nand_50_out, nand_51_out,
       nand_52_out, nand_53_out, nand_54_out, nand_55_out, nand_56_out, nand_57_out, nand_58_out,
       nand_59_out, nand_60_out, nand_61_out, nand_62_out, nand_63_out, nand_64_out, nand_65_out,
       nand_66_out, nand_67_out, nand_68_out, nand_69_out, nand_70_out, nand_71_out, nand_72_out,
       nand_73_out, nand_74_out, nand_75_out, nand_76_out, nand_77_out, nand_78_out, nand_79_out,
       nand_80_out, nand_81_out, nand_82_out, nand_83_out, nand_84_out, nand_85_out, nand_86_out,
       nand_87_out, nand_88_out, nand_89_out, nand_90_out, nand_91_out, nand_92_out, nand_93_out,
       nand_94_out, nand_95_out, nand_96_out, nand_97_out, nand_98_out, nand_99_out, nand_100_out,
       nand_101_out, nand_102_out, nand_103_out, nand_104_out, nand_106_out, nand_107_out, nand_108_out,
       nand_109_out, nand_110_out, nand_111_out, nand_112_out, nand_113_out, nand_114_out, nand_115_out,
       nand_116_out, nand_117_out, nand_118_out, nand_119_out, nand_120_out, nand_121_out, nand_122_out,
       nand_123_out, nand_124_out, nand_125_out, nand_126_out, nand_127_out, nand_128_out, nand_129_out,
       nand_130_out, nand_131_out, nand_132_out, nand_133_out, nand_134_out, nand_136_out, nand_137_out,
       nand_138_out, nand_139_out, nand_141_out, nand_142_out, nand_143_out, nand_144_out, nand_145_out,
       nand_146_out, nand_147_out, nand_148_out;

  nand nand_1 (nand_1_out, C, C);
  nand nand_2 (nand_2_out, D, D);
  nand nand_3 (nand_3_out, B, B);
  nand nand_4 (nand_4_out, D, D);
  nand nand_5 (nand_5_out, B, B);
  nand nand_6 (nand_6_out, D, D);
  nand nand_7 (nand_7_out, D, D);
  nand nand_8 (nand_8_out, C, C);
  nand nand_9 (nand_9_out, C, C);
  nand nand_10 (nand_10_out, C, C);
  nand nand_11 (nand_11_out, A, A);
  nand nand_12 (nand_12_out, A, A);
  nand nand_13 (nand_13_out, D, D);
  nand nand_14 (nand_14_out, C, C);
  nand nand_15 (nand_15_out, A, A);
  nand nand_16 (nand_16_out, D, D);
  nand nand_17 (nand_17_out, D, nand_1_out);
  nand nand_18 (nand_18_out, nand_2_out, nand_3_out);
  nand nand_19 (nand_19_out, nand_4_out, nand_5_out);
  nand nand_20 (nand_20_out, nand_6_out, A);
  nand nand_21 (nand_21_out, nand_7_out, nand_8_out);
  nand nand_22 (nand_22_out, nand_9_out, B);
  nand nand_23 (nand_23_out, nand_10_out, nand_11_out);
  nand nand_24 (nand_24_out, B, nand_12_out);
  nand nand_25 (nand_25_out, D, B);
  nand nand_26 (nand_26_out, D, C);
  nand nand_27 (nand_27_out, nand_13_out, C);
  nand nand_28 (nand_28_out, nand_14_out, B);
  nand nand_29 (nand_29_out, B, nand_15_out);
  nand nand_30 (nand_30_out, nand_16_out, C);
  nand nand_31 (nand_31_out, C, C);
  nand nand_32 (nand_32_out, A, A);
  nand nand_33 (nand_33_out, D, D);
  nand nand_34 (nand_34_out, D, D);
  nand nand_35 (nand_35_out, nand_17_out, nand_17_out);
  nand nand_36 (nand_36_out, B, B);
  nand nand_37 (nand_37_out, D, D);
  nand nand_38 (nand_38_out, C, C);
  nand nand_39 (nand_39_out, nand_18_out, nand_18_out);
  nand nand_40 (nand_40_out, A, A);
  nand nand_41 (nand_41_out, D, D);
  nand nand_42 (nand_42_out, B, B);
  nand nand_43 (nand_43_out, nand_19_out, nand_20_out);
  nand nand_44 (nand_44_out, B, B);
  nand nand_45 (nand_45_out, D, D);
  nand nand_46 (nand_46_out, C, C);
  nand nand_47 (nand_47_out, nand_21_out, nand_21_out);
  nand nand_48 (nand_48_out, A, A);
  nand nand_49 (nand_49_out, nand_22_out, nand_22_out);
  nand nand_50 (nand_50_out, B, B);
  nand nand_51 (nand_51_out, B, B);
  nand nand_52 (nand_52_out, nand_23_out, nand_24_out);
  nand nand_53 (nand_53_out, nand_25_out, nand_26_out);
  nand nand_54 (nand_54_out, B, B);
  nand nand_55 (nand_55_out, A, A);
  nand nand_56 (nand_56_out, nand_27_out, nand_27_out);
  nand nand_57 (nand_57_out, B, B);
  nand nand_58 (nand_58_out, nand_28_out, nand_29_out);
  nand nand_59 (nand_59_out, nand_30_out, nand_30_out);
  nand nand_60 (nand_60_out, B, B);
  nand nand_61 (nand_61_out, C, C);
  nand nand_62 (nand_62_out, nand_31_out, nand_32_out);
  nand nand_63 (nand_63_out, nand_33_out, B);
  nand nand_64 (nand_64_out, nand_34_out, C);
  nand nand_65 (nand_65_out, C, B);
  nand nand_66 (nand_66_out, nand_35_out, nand_36_out);
  nand nand_67 (nand_67_out, nand_37_out, nand_38_out);
  nand nand_68 (nand_68_out, nand_39_out, nand_40_out);
  nand nand_69 (nand_69_out, nand_41_out, B);
  nand nand_70 (nand_70_out, D, nand_42_out);
  nand nand_71 (nand_71_out, nand_43_out, nand_43_out);
  nand nand_72 (nand_72_out, nand_44_out, A);
  nand nand_73 (nand_73_out, nand_45_out, C);
  nand nand_74 (nand_74_out, D, nand_46_out);
  nand nand_75 (nand_75_out, nand_47_out, nand_48_out);
  nand nand_76 (nand_76_out, nand_49_out, A);
  nand nand_77 (nand_77_out, C, nand_50_out);
  nand nand_78 (nand_78_out, C, B);
  nand nand_79 (nand_79_out, D, nand_51_out);
  nand nand_80 (nand_80_out, nand_52_out, nand_52_out);
  nand nand_81 (nand_81_out, nand_53_out, nand_53_out);
  nand nand_82 (nand_82_out, nand_54_out, nand_55_out);
  nand nand_83 (nand_83_out, nand_56_out, nand_57_out);
  nand nand_84 (nand_84_out, nand_58_out, nand_58_out);
  nand nand_85 (nand_85_out, nand_59_out, nand_60_out);
  nand nand_86 (nand_86_out, D, nand_61_out);
  nand nand_87 (nand_87_out, D, A);
  nand nand_88 (nand_88_out, nand_62_out, nand_63_out);
  nand nand_89 (nand_89_out, nand_64_out, nand_64_out);
  nand nand_90 (nand_90_out, nand_65_out, nand_66_out);
  nand nand_91 (nand_91_out, A, A);
  nand nand_92 (nand_92_out, nand_67_out, nand_68_out);
  nand nand_93 (nand_93_out, C, C);
  nand nand_94 (nand_94_out, A, A);
  nand nand_95 (nand_95_out, nand_69_out, nand_69_out);
  nand nand_96 (nand_96_out, nand_70_out, nand_70_out);
  nand nand_97 (nand_97_out, nand_71_out, nand_72_out);
  nand nand_98 (nand_98_out, nand_73_out, nand_74_out);
  nand nand_99 (nand_99_out, nand_75_out, nand_76_out);
  nand nand_100 (nand_100_out, nand_77_out, nand_77_out);
  nand nand_101 (nand_101_out, nand_78_out, nand_78_out);
  nand nand_102 (nand_102_out, A, A);
  nand nand_103 (nand_103_out, nand_79_out, nand_79_out);
  nand nand_104 (nand_104_out, A, A);
  nand nand_105 (e, nand_80_out, nand_81_out);
  nand nand_106 (nand_106_out, nand_82_out, nand_83_out);
  nand nand_107 (nand_107_out, A, A);
  nand nand_108 (nand_108_out, C, C);
  nand nand_109 (nand_109_out, nand_84_out, nand_85_out);
  nand nand_110 (nand_110_out, nand_86_out, nand_87_out);
  nand nand_111 (nand_111_out, nand_88_out, nand_88_out);
  nand nand_112 (nand_112_out, nand_89_out, A);
  nand nand_113 (nand_113_out, nand_90_out, nand_90_out);
  nand nand_114 (nand_114_out, D, nand_91_out);
  nand nand_115 (nand_115_out, nand_92_out, nand_92_out);
  nand nand_116 (nand_116_out, nand_93_out, nand_94_out);
  nand nand_117 (nand_117_out, nand_95_out, A);
  nand nand_118 (nand_118_out, nand_96_out, A);
  nand nand_119 (nand_119_out, nand_97_out, nand_97_out);
  nand nand_120 (nand_120_out, nand_98_out, nand_98_out);
  nand nand_121 (nand_121_out, nand_99_out, nand_99_out);
  nand nand_122 (nand_122_out, nand_100_out, A);
  nand nand_123 (nand_123_out, nand_101_out, nand_102_out);
  nand nand_124 (nand_124_out, nand_103_out, nand_104_out);
  nand nand_125 (nand_125_out, nand_106_out, nand_106_out);
  nand nand_126 (nand_126_out, C, nand_107_out);
  nand nand_127 (nand_127_out, D, nand_108_out);
  nand nand_128 (nand_128_out, D, B);
  nand nand_129 (nand_129_out, nand_109_out, nand_109_out);
  nand nand_130 (nand_130_out, nand_110_out, nand_110_out);
  nand nand_131 (nand_131_out, nand_111_out, nand_112_out);
  nand nand_132 (nand_132_out, nand_113_out, nand_114_out);
  nand nand_133 (nand_133_out, nand_115_out, nand_116_out);
  nand nand_134 (nand_134_out, nand_117_out, nand_118_out);
  nand nand_135 (c_2, nand_119_out, nand_120_out);
  nand nand_136 (nand_136_out, nand_121_out, nand_122_out);
  nand nand_137 (nand_137_out, nand_123_out, nand_124_out);
  nand nand_138 (nand_138_out, nand_125_out, nand_126_out);
  nand nand_139 (nand_139_out, nand_127_out, nand_128_out);
  nand nand_140 (g, nand_129_out, nand_130_out);
  nand nand_141 (nand_141_out, nand_131_out, nand_131_out);
  nand nand_142 (nand_142_out, nand_132_out, nand_132_out);
  nand nand_143 (nand_143_out, nand_133_out, nand_133_out);
  nand nand_144 (nand_144_out, nand_134_out, nand_134_out);
  nand nand_145 (nand_145_out, nand_136_out, nand_136_out);
  nand nand_146 (nand_146_out, nand_137_out, nand_137_out);
  nand nand_147 (nand_147_out, nand_138_out, nand_138_out);
  nand nand_148 (nand_148_out, nand_139_out, nand_139_out);
  nand nand_149 (a_2, nand_141_out, nand_142_out);
  nand nand_150 (b_2, nand_143_out, nand_144_out);
  nand nand_151 (d_2, nand_145_out, nand_146_out);
  nand nand_152 (f, nand_147_out, nand_148_out);
endmodule

module Gravity (
  input  [3:0] in_1,
  input  in_2,
  output out_3
);

  wire and_1_out, comparator_1_eq, comparator_2_eq, d_ff_1_qn, or_1_out;

  Comparator #(.width(4)) comparator_1 (.a(in_1), .b(4'b1001), .eq(comparator_1_eq));  // open: gt, lt
  Comparator #(.width(4)) comparator_2 (.a(in_1), .b(4'b0100), .eq(comparator_2_eq));  // open: gt, lt
  or or_1 (or_1_out, comparator_2_eq, comparator_1_eq);
  and and_1 (and_1_out, or_1_out, d_ff_1_qn);
  D_Flip_Flop #(.trigger("falling")) d_ff_1 (
    .clk(or_1_out), .D(and_1_out), .Q(out_3), .Qn(d_ff_1_qn), .reset(in_2));  // open: preset, en

  // Notes on the sheet:
  //   The second digit counter
endmodule

module GameOverModule (
  input  in_1,
  output [23:0] out_2,
  output [23:0] out_3,
  output [23:0] out_4,
  output [23:0] out_5,
  output [23:0] out_6,
  output [23:0] out_7,
  output [23:0] out_8,
  output [23:0] out_9,
  output [23:0] out_10,
  output [23:0] out_11,
  output [23:0] out_12
);

  wire not_1_out, not_2_out, not_3_out, not_4_out, not_5_out, not_6_out, not_7_out, not_8_out, not_9_out,
       not_10_out, not_11_out, not_12_out;
  wire [23:0] controlled_buffer_1_out, controlled_buffer_2_out, controlled_buffer_3_out,
       controlled_buffer_4_out, controlled_buffer_5_out, controlled_buffer_8_out, controlled_buffer_10_out,
       controlled_buffer_12_out, controlled_buffer_17_out, controlled_buffer_19_out, controlled_buffer_21_out;

  assign controlled_buffer_1_out = not_1_out ? 24'h3c444e : 24'bz;  // Controlled_Buffer controlled_buffer_1
  not not_1 (not_1_out, not_12_out);
  assign controlled_buffer_2_out = not_2_out ? 24'h20a6c8 : 24'bz;  // Controlled_Buffer controlled_buffer_2
  not not_2 (not_2_out, not_12_out);
  not not_3 (not_3_out, not_12_out);
  assign controlled_buffer_3_out = not_4_out ? {24{1'b0}} : 24'bz;  // Controlled_Buffer controlled_buffer_3
  not not_4 (not_4_out, not_12_out);
  assign controlled_buffer_4_out = not_5_out ? 24'h191738 : 24'bz;  // Controlled_Buffer controlled_buffer_4
  not not_5 (not_5_out, not_12_out);
  assign controlled_buffer_5_out = not_6_out ? 24'h251424 : 24'bz;  // Controlled_Buffer controlled_buffer_5
  not not_6 (not_6_out, not_12_out);
  not not_7 (not_7_out, not_12_out);
  Adder #(.width(24)) adder_1 (.a({24{1'b0}}), .b(controlled_buffer_1_out), .out(out_2));  // open: cin, cout
  assign controlled_buffer_1_out = not_12_out ? {24{1'b0}} : 24'bz;  // Controlled_Buffer controlled_buffer_6
  assign controlled_buffer_2_out = not_12_out ? {24{1'b0}} : 24'bz;  // Controlled_Buffer controlled_buffer_7
  assign controlled_buffer_8_out = not_12_out ? {24{1'b0}} : 24'bz;  // Controlled_Buffer controlled_buffer_8
  assign controlled_buffer_8_out = not_3_out ? 24'h2ca54c : 24'bz;  // Controlled_Buffer controlled_buffer_9
  assign controlled_buffer_10_out = not_12_out ? {24{1'b0}} : 24'bz;  // Controlled_Buffer controlled_buffer_10
  assign controlled_buffer_10_out = not_8_out ? 24'h24e448 : 24'bz;  // Controlled_Buffer controlled_buffer_11
  not not_8 (not_8_out, not_12_out);
  assign controlled_buffer_12_out = not_12_out ? {24{1'b0}} : 24'bz;  // Controlled_Buffer controlled_buffer_12
  assign controlled_buffer_12_out = not_9_out ? 24'h3ca44e : 24'bz;  // Controlled_Buffer controlled_buffer_13
  not not_9 (not_9_out, not_12_out);
  assign controlled_buffer_3_out = not_12_out ? {24{1'b0}} : 24'bz;  // Controlled_Buffer controlled_buffer_14
  Adder #(.width(24)) adder_2 (.a({24{1'b0}}), .b(controlled_buffer_4_out), .out(out_8));  // open: cin, cout
  assign controlled_buffer_4_out = not_12_out ? {24{1'b0}} : 24'bz;  // Controlled_Buffer controlled_buffer_15
  assign controlled_buffer_5_out = not_12_out ? {24{1'b0}} : 24'bz;  // Controlled_Buffer controlled_buffer_16
  assign controlled_buffer_17_out = not_12_out ? {24{1'b0}} : 24'bz;  // Controlled_Buffer controlled_buffer_17
  assign controlled_buffer_17_out = not_7_out ? 24'h24a638 : 24'bz;  // Controlled_Buffer controlled_buffer_18
  assign controlled_buffer_19_out = not_12_out ? {24{1'b0}} : 24'bz;  // Controlled_Buffer controlled_buffer_19
  assign controlled_buffer_19_out = not_10_out ? 24'h24a424 : 24'bz;  // Controlled_Buffer controlled_buffer_20
  not not_10 (not_10_out, not_12_out);
  assign controlled_buffer_21_out = not_12_out ? {24{1'b0}} : 24'bz;  // Controlled_Buffer controlled_buffer_21
  assign controlled_buffer_21_out = not_11_out ? 24'h184724 : 24'bz;  // Controlled_Buffer controlled_buffer_22
  not not_11 (not_11_out, not_12_out);
  not not_12 (not_12_out, in_1);
  Adder #(.width(24)) adder_3 (.a({24{1'b0}}), .b(controlled_buffer_2_out), .out(out_3));  // open: cin, cout
  Adder #(.width(24)) adder_4 (.a({24{1'b0}}), .b(controlled_buffer_8_out), .out(out_4));  // open: cin, cout
  Adder #(.width(24)) adder_5 (.a({24{1'b0}}), .b(controlled_buffer_10_out), .out(out_5));  // open: cin, cout
  Adder #(.width(24)) adder_6 (.a({24{1'b0}}), .b(controlled_buffer_12_out), .out(out_6));  // open: cin, cout
  Adder #(.width(24)) adder_7 (.a({24{1'b0}}), .b(controlled_buffer_3_out), .out(out_7));  // open: cin, cout
  Adder #(.width(24)) adder_8 (.a({24{1'b0}}), .b(controlled_buffer_5_out), .out(out_9));  // open: cin, cout
  Adder #(.width(24)) adder_9 (.a({24{1'b0}}), .b(controlled_buffer_17_out), .out(out_10));  // open: cin, cout
  Adder #(.width(24)) adder_10 (.a({24{1'b0}}), .b(controlled_buffer_19_out), .out(out_11));  // open: cin, cout
  Adder #(.width(24)) adder_11 (.a({24{1'b0}}), .b(controlled_buffer_21_out), .out(out_12));  // open: cin, cout

  // Notes on the sheet:
  //   problem 5
endmodule

module Gravity_Selector (
  input  [23:0] in_1,
  input  [23:0] in_2,
  input  [23:0] in_3,
  input  [23:0] in_4,
  input  [23:0] in_5,
  input  in_6,
  output [23:0] out_7,
  output [23:0] out_8,
  output [23:0] out_9,
  output [23:0] out_10,
  output [23:0] out_11
);

  wire not_1_out, not_2_out, not_3_out, not_4_out, not_5_out;
  wire [23:0] controlled_buffer_1_out, controlled_buffer_3_out, controlled_buffer_5_out,
       controlled_buffer_7_out, controlled_buffer_9_out;

  assign controlled_buffer_1_out = not_1_out ? in_1 : 24'bz;  // Controlled_Buffer controlled_buffer_1
  not not_1 (not_1_out, in_6);
  not not_2 (not_2_out, in_6);
  assign controlled_buffer_1_out = in_6 ? {24{1'b0}} : 24'bz;  // Controlled_Buffer controlled_buffer_2
  assign controlled_buffer_3_out = in_6 ? {24{1'b0}} : 24'bz;  // Controlled_Buffer controlled_buffer_3
  assign controlled_buffer_3_out = not_2_out ? in_2 : 24'bz;  // Controlled_Buffer controlled_buffer_4
  assign controlled_buffer_5_out = in_6 ? {24{1'b0}} : 24'bz;  // Controlled_Buffer controlled_buffer_5
  assign controlled_buffer_5_out = not_3_out ? in_3 : 24'bz;  // Controlled_Buffer controlled_buffer_6
  not not_3 (not_3_out, in_6);
  assign controlled_buffer_7_out = in_6 ? {24{1'b0}} : 24'bz;  // Controlled_Buffer controlled_buffer_7
  assign controlled_buffer_7_out = not_4_out ? in_4 : 24'bz;  // Controlled_Buffer controlled_buffer_8
  not not_4 (not_4_out, in_6);
  assign controlled_buffer_9_out = in_6 ? {24{1'b0}} : 24'bz;  // Controlled_Buffer controlled_buffer_9
  assign controlled_buffer_9_out = not_5_out ? in_5 : 24'bz;  // Controlled_Buffer controlled_buffer_10
  not not_5 (not_5_out, in_6);
  Adder #(.width(24)) adder_1 (.a({24{1'b0}}), .b(controlled_buffer_1_out), .out(out_7));  // open: cin, cout
  Adder #(.width(24)) adder_2 (.a({24{1'b0}}), .b(controlled_buffer_3_out), .out(out_8));  // open: cin, cout
  Adder #(.width(24)) adder_3 (.a({24{1'b0}}), .b(controlled_buffer_5_out), .out(out_9));  // open: cin, cout
  Adder #(.width(24)) adder_4 (.a({24{1'b0}}), .b(controlled_buffer_7_out), .out(out_10));  // open: cin, cout
  Adder #(.width(24)) adder_5 (.a({24{1'b0}}), .b(controlled_buffer_9_out), .out(out_11));  // open: cin, cout
endmodule

module ScoreStopper (
  input  [3:0] in_1,
  output out_2
);

  Comparator #(.width(4)) comparator_1 (.a(in_1), .b(4'b1010), .eq(out_2));  // open: gt, lt

  // Notes on the sheet:
  //   The second digit counter
endmodule
